// Logisim project ALU.circ as structural Verilog: 7 circuits, main circuit Add1bit
module Add1bit (
  input  A_in,
  input  B_in,
  input  C_in,
  output S,
  output C_out
);

  wire and_1_out, and_2_out, and_3_out, xor_1_out;

  xor xor_1 (xor_1_out, A_in, B_in);
  and and_1 (and_1_out, A_in, B_in);
  and and_2 (and_2_out, A_in, C_in);
  and and_3 (and_3_out, B_in, C_in);
  xor xor_2 (S, xor_1_out, C_in);
  or or_1 (C_out, and_1_out, and_2_out, and_3_out);
endmodule

module Add4bit (
  input  C_in,
  input  [3:0] A_in,
  input  [3:0] B_in,
  output [3:0] S,
  output C_out
);

  wire add1bit_1_c_out, add1bit_2_c_out, add1bit_3_c_out;

  Add1bit add1bit_1 (.A_in(A_in[0]), .B_in(B_in[0]), .C_in(C_in), .S(S[0]), .C_out(add1bit_1_c_out));
  Add1bit add1bit_2 (.A_in(A_in[1]), .B_in(B_in[1]), .C_in(add1bit_1_c_out), .S(S[1]), .C_out(add1bit_2_c_out));
  Add1bit add1bit_3 (.A_in(A_in[2]), .B_in(B_in[2]), .C_in(add1bit_2_c_out), .S(S[2]), .C_out(add1bit_3_c_out));
  Add1bit add1bit_4 (.A_in(A_in[3]), .B_in(B_in[3]), .C_in(add1bit_3_c_out), .S(S[3]), .C_out(C_out));
endmodule

module Add8bit (
  input  C_in,
  input  [7:0] A,
  input  [7:0] B,
  output [7:0] S,
  output C_out
);

  wire add4bit_1_c_out;

  Add4bit add4bit_1 (.C_in(C_in), .A_in(A[3:0]), .B_in(B[3:0]), .S(S[3:0]), .C_out(add4bit_1_c_out));
  Add4bit add4bit_2 (.C_in(add4bit_1_c_out), .A_in(A[7:4]), .B_in(B[7:4]), .S(S[7:4]), .C_out(C_out));
endmodule

module ALU_complexe (
  input  [2:0] Operateur,
  input  [7:0] A_in,
  input  [7:0] B_in,
  output V_out,
  output C_out,
  output N_out,
  output Z_out,
  output [7:0] S
);

  wire [7:0] alu_simple_1_s, and_1_out, not_1_out, or_1_out;

  assign and_1_out = A_in & B_in;  // AND_Gate and_1, 8 bits wide
  assign or_1_out = A_in | B_in;  // OR_Gate or_1, 8 bits wide
  assign not_1_out = ~A_in;  // NOT_Gate not_1, 8 bits wide
  ALU_simple alu_simple_1 (
    .A_in(A_in), .B_in(B_in), .Operateur(Operateur[0]), .S(alu_simple_1_s), .C_out(C_out), .Z_out(Z_out),
    .N_out(N_out), .V_out(V_out));
  Multiplexer #(.select(3), .width(8)) multiplexer_1 (
    .in0(alu_simple_1_s), .in1(alu_simple_1_s), .in2({A_in[6:0], 1'b0}), .in3({1'b0, A_in[7:1]}),
    .in4({{2{A_in[7]}}, A_in[6:1]}), .in5(and_1_out), .in6(or_1_out), .in7(not_1_out), .out(S),
    .sel(Operateur));  // open: en
endmodule

module ALU_simple (
  input  [7:0] A_in,
  input  [7:0] B_in,
  input  Operateur,
  output [7:0] S,
  output C_out,
  output Z_out,
  output N_out,
  output V_out
);

  wire and_1_out, and_2_out, not_2_out, not_3_out, not_4_out;
  wire [7:0] multiplexer_1_out, not_1_out;

  // Probe on A_in
  // Probe on B_in
  Multiplexer #(.width(8), .enable("false")) multiplexer_1 (
    .in0(B_in), .in1(not_1_out), .out(multiplexer_1_out), .sel(Operateur));
  assign not_1_out = ~B_in;  // NOT_Gate not_1, 8 bits wide
  Add8bit Additionneur (.C_in(Operateur), .A(A_in), .B(multiplexer_1_out), .S({N_out, S[6:0]}), .C_out(C_out));
  not not_2 (not_2_out, N_out);
  and and_1 (and_1_out, not_2_out, A_in[7], multiplexer_1_out[7]);
  not not_3 (not_3_out, A_in[7]);
  and and_2 (and_2_out, N_out, not_3_out, not_4_out);
  not not_4 (not_4_out, multiplexer_1_out[7]);
  // Probe on {N_out, S[6:0]}
  or or_1 (V_out, and_1_out, and_2_out);
  and and_3 (Z_out, ~S[0], ~S[1], ~S[2], ~S[3], ~S[4], ~S[5], ~S[6], ~N_out);  // AND_Gate

  assign S[7] = N_out;
endmodule

module Table_de_mixage (
  input  [1:0] CtrlA,
  input  [7:0] A,
  input  [1:0] CtrlB,
  input  [7:0] B,
  output [7:0] S
);

  wire alu_complexe_3_n_out, alu_complexe_3_z_out, and_1_out;
  wire [7:0] alu_complexe_1_s, alu_complexe_2_s, alu_complexe_3_s, multiplexer_2_out;

  ALU_complexe alu_complexe_1 (
    .Operateur({CtrlA, 1'b0}), .A_in(A), .S(alu_complexe_1_s));  // open: B_in, V_out, C_out, N_out, Z_out
  ALU_complexe alu_complexe_2 (
    .Operateur({CtrlB, 1'b0}), .A_in(B), .S(alu_complexe_2_s));  // open: B_in, V_out, C_out, N_out, Z_out
  // Probe on alu_complexe_1_s
  // Probe on alu_complexe_2_s
  ALU_complexe alu_complexe_3 (
    .Operateur(3'b000), .A_in(alu_complexe_1_s), .B_in(alu_complexe_2_s), .N_out(alu_complexe_3_n_out),
    .Z_out(alu_complexe_3_z_out), .S(alu_complexe_3_s));  // open: V_out, C_out
  and and_1 (and_1_out, alu_complexe_3_n_out, alu_complexe_3_z_out);
  Multiplexer #(.width(8), .enable("false")) multiplexer_1 (
    .in0(alu_complexe_3_s), .in1(multiplexer_2_out), .out(S), .sel(alu_complexe_3_z_out));
  Multiplexer #(.width(8), .enable("false")) multiplexer_2 (
    .in0(8'h7f), .in1(8'h80), .out(multiplexer_2_out), .sel(and_1_out));
  // Probe on S
endmodule

module Valeur_Absolue (
  input  C_in,
  input  [7:0] A,
  input  [7:0] B,
  output [7:0] S
);

  wire comparator_1_gt;
  wire [7:0] add8bit_1_p5, add8bit_2_p2, add8bit_2_p4, multiplexer_1_out, not_1_out;

  Multiplexer #(.width(8), .enable("false")) multiplexer_1 (
    .in0(B), .in1(not_1_out), .out(multiplexer_1_out), .sel(C_in));
  assign not_1_out = ~B;  // NOT_Gate not_1, 8 bits wide
  // Add8bit add8bit_1: pin names not known; wires that end beside it: B, C_in, A, multiplexer_1_out, add8bit_1_p5
  // Add8bit add8bit_2: pin names not known; wires that end beside it: 1'b0, add8bit_2_p2, 8'h1, add8bit_2_p4
  assign add8bit_2_p2 = ~add8bit_1_p5;  // NOT_Gate not_2, 8 bits wide
  Comparator comparator_1 (.a(add8bit_1_p5), .b({8{1'b0}}), .gt(comparator_1_gt));  // open: eq, lt
  Multiplexer #(.width(8), .enable("false")) multiplexer_2 (
    .in0(add8bit_2_p4), .in1(add8bit_1_p5), .out(S), .sel(comparator_1_gt));
endmodule
