// Logisim project Projet.circ as structural Verilog: 10 circuits, main circuit main
module main (
  input  reset
);

  wire clk_out, down_out, sysclk_out, up_out;
  wire [2:0] rgb_video_1_p7;
  wire [3:0] rgb_video_1_p5, rgb_video_1_p6;

  Clock sysclk (.out(sysclk_out));
  Clock clk (.out(clk_out));
  Button up (.out(up_out));
  Button down (.out(down_out));
  // RGB_Video #(.reset("Synchronous"), .width(16), .height(16), .scale(8)) rgb_video_1: pin names not known; wires that end beside it: sysclk_out, reset, clk_out, 1'b1, rgb_video_1_p5, rgb_video_1_p6, rgb_video_1_p7
  jeu jeu_1 (
    .clk(clk_out), .rst(reset), .up(up_out), .down(down_out), .v_sync(rgb_video_1_p6),
    .h_sync(rgb_video_1_p5), .pixel(rgb_video_1_p7));
endmodule

module banque_registres (
  input  reset,
  input  [7:0] data,
  input  clk,
  input  [2:0] addr_A,
  input  [2:0] addr_data,
  input  [2:0] addr_B,
  input  en,
  output [7:0] S1,
  output [7:0] S2,
  output [7:0] R0,
  output [7:0] R1,
  output [7:0] R2,
  output [7:0] R3,
  output [7:0] R4,
  output [7:0] R5,
  output [7:0] R6,
  output [7:0] R7
);

  wire E0, E1, E2, E3, E4, E5, E6, E7;

  Decoder #(.select(3)) decoder_1 (
    .out0(E0), .out1(E1), .out2(E2), .out3(E3), .out4(E4), .out5(E5), .out6(E6), .out7(E7), .sel(addr_data),
    .en(en));
  registre registre_1 (.data(data), .en(E0), .clk(clk), .reset(reset), .S(R0));
  registre registre_2 (.data(data), .en(E1), .clk(clk), .reset(reset), .S(R1));
  registre registre_3 (.data(data), .en(E2), .clk(clk), .reset(reset), .S(R2));
  registre registre_4 (.data(data), .en(E3), .clk(clk), .reset(reset), .S(R3));
  registre registre_5 (.data(data), .en(E4), .clk(clk), .reset(reset), .S(R4));
  registre registre_6 (.data(data), .en(E5), .clk(clk), .reset(reset), .S(R5));
  registre registre_7 (.data(data), .en(E6), .clk(clk), .reset(reset), .S(R6));
  registre registre_8 (.data(data), .en(E7), .clk(clk), .reset(reset), .S(R7));
  Multiplexer #(.select(3), .width(8), .enable("false")) multiplexer_1 (
    .in0(R0), .in1(R1), .in2(R2), .in3(R3), .in4(R4), .in5(R5), .in6(R6), .in7(R7), .out(S1), .sel(addr_A));
  Multiplexer #(.select(3), .width(8), .enable("false")) multiplexer_2 (
    .in0(R0), .in1(R1), .in2(R2), .in3(R3), .in4(R4), .in5(R5), .in6(R6), .in7(R7), .out(S2), .sel(addr_B));

  // Other names for the same wires on the sheet: A[2:0] = addr_A; B[2:0] = addr_B; rst = reset
endmodule

module registre (
  input  [7:0] data,
  input  en,
  input  clk,
  input  reset,
  output [7:0] S
);

  Register register_1 (.D(data), .en(en), .clk(clk), .Q(S), .clr(reset));
endmodule

module unite_controle (
  input  [3:0] opcode,
  input  [3:0] condition,
  input  [3:0] fanions,
  output [1:0] select_data,
  output [1:0] select_addr,
  output sauter,
  output write_en,
  output read_data,
  output w_en_data
);

  wire and_1_out, and_2_out, and_3_out, and_4_out, and_5_out, and_6_out, and_9_out, and_10_out, and_12_out,
       or_1_out, or_5_out;

  and and_1 (and_1_out, condition[0], fanions[0]);
  and and_2 (and_2_out, condition[1], fanions[1]);
  and and_3 (and_3_out, condition[2], fanions[2]);
  and and_4 (and_4_out, condition[3], fanions[3]);
  or or_1 (or_1_out, and_1_out, and_2_out, and_3_out, and_4_out);
  and and_5 (and_5_out, ~opcode[0], ~opcode[1], ~opcode[2], opcode[3]);  // AND_Gate
  and and_6 (and_6_out, opcode[0], opcode[1], ~opcode[2], opcode[3]);  // AND_Gate
  and and_7 (select_addr[0], ~opcode[0], opcode[1], opcode[2], opcode[3]);  // AND_Gate
  and and_8 (select_addr[1], opcode[0], opcode[1], opcode[2], opcode[3]);
  and and_9 (and_9_out, ~opcode[0], opcode[1], ~opcode[2], opcode[3]);  // AND_Gate
  and and_10 (and_10_out, ~opcode[0], ~opcode[1], opcode[2], opcode[3]);  // AND_Gate
  and and_11 (w_en_data, opcode[0], ~opcode[1], opcode[2], opcode[3]);  // AND_Gate
  and and_12 (and_12_out, or_1_out, and_9_out);
  or or_2 (select_data[0], and_5_out, and_10_out);
  or or_3 (select_data[1], and_10_out, select_addr[0]);
  or or_4 (sauter, and_6_out, select_addr[0], select_addr[1], and_12_out);
  or or_5 (or_5_out, and_6_out, select_addr[1], and_9_out, w_en_data);
  or or_6 (read_data, select_addr[1], and_10_out, w_en_data);
  not not_1 (write_en, or_5_out);
endmodule

module cpu (
  input  clk,
  input  rst,
  input  [7:0] data_in,
  output [7:0] addr_out,
  output w_en,
  output [7:0] data_out
);

  wire not_1_out, read_data, sauter, w_en_t;
  wire [1:0] S0, s_addr, s_data;
  wire [2:0] multiplexer_3_out, S1, val;
  wire [3:0] alu_complexe_1_p10, condition, opcode, register_1_q;
  wire [7:0] banque_registres_1_r0, banque_registres_1_r1, banque_registres_1_r2, banque_registres_1_r3,
       banque_registres_1_r4, banque_registres_1_r5, banque_registres_1_r6, banque_registres_1_r7,
       banque_registres_1_s1, counter_1_q, data, multiplexer_1_out, multiplexer_2_out, RL, val_saut;

  Multiplexer #(.select(2), .width(8), .enable("false")) multiplexer_1 (
    .in0(val_saut), .in1({S0, S1, val}), .in2(data_out), .out(multiplexer_1_out), .sel(s_addr));  // open: in3
  Multiplexer #(.select(2), .width(8), .enable("false")) multiplexer_2 (
    .in0(data), .in1({S0, S1, val}), .in2(RL), .in3(data_in), .out(multiplexer_2_out), .sel(s_data));
  not not_1 (not_1_out, read_data);
  Counter counter_1 (
    .load(sauter), .up(1'b1), .count(1'b1), .clk(clk), .D(multiplexer_1_out), .Q(counter_1_q));  // open: clr, carry
  Multiplexer #(.width(3), .enable("false")) multiplexer_3 (
    .in0(condition[3:1]), .in1(S1), .out(multiplexer_3_out), .sel(not_1_out));
  banque_registres banque_registres_1 (
    .reset(rst), .data(multiplexer_2_out), .clk(clk), .addr_A({condition[0], S0}),
    .addr_data(condition[3:1]), .addr_B(multiplexer_3_out), .en(w_en_t), .S1(banque_registres_1_s1),
    .S2(data_out), .R0(banque_registres_1_r0), .R1(banque_registres_1_r1), .R2(banque_registres_1_r2),
    .R3(banque_registres_1_r3), .R4(banque_registres_1_r4), .R5(banque_registres_1_r5),
    .R6(banque_registres_1_r6), .R7(banque_registres_1_r7));
  // Probe on banque_registres_1_r0
  // Probe on banque_registres_1_r1
  // Probe on banque_registres_1_r2
  // Probe on banque_registres_1_r3
  // Probe on banque_registres_1_r4
  // Probe on banque_registres_1_r5
  // Probe on banque_registres_1_r6
  // Probe on banque_registres_1_r7
  Adder adder_1 (.a({S0, S1, val}), .b(counter_1_q), .out(val_saut));  // open: cin, cout
  Adder adder_2 (.a(counter_1_q), .b(8'h1), .out(RL));  // open: cin, cout
  // Probe on condition[3:1]
  // Probe on {S0, S1, val}
  // Probe on {opcode, condition, S0, S1, val}
  // ALU_complexe alu_complexe_1: pin names not known; wires that end beside it: opcode[2:0], banque_registres_1_s1, 16'h8810, 16'h8a01, 16'h8000, {16{1'b0}}, 16'h8200, 16'h8401, {16{1'b0}}, alu_complexe_1_p10[0], alu_complexe_1_p10[1], alu_complexe_1_p10[2], alu_complexe_1_p10[3], data
  // Probe on {condition[0], S0}
  mem_rom mem_rom_1 (.addr(counter_1_q[6:0]), .instruction({opcode, condition, S0, S1, val}));
  // Probe on {opcode, condition, S0, S1, val}
  // Probe on S1
  // Probe on condition
  Adder adder_3 (.a({2'b00, S1, val}), .b(banque_registres_1_s1), .out(addr_out));  // open: cin, cout
  Register #(.width(4)) register_1 (.D(alu_complexe_1_p10), .en(1'b1), .clk(clk), .Q(register_1_q));  // open: clr
  // Probe on data
  // Probe on opcode
  unite_controle unite_controle_1 (
    .opcode(opcode), .condition(condition), .fanions(register_1_q), .select_data(s_data),
    .select_addr(s_addr), .sauter(sauter), .write_en(w_en_t), .read_data(read_data), .w_en_data(w_en));

  // Other names for the same wires on the sheet: val[7:3] = {S0, S1}; S0[2] = condition[0];
  //   result[2:0] = condition[3:1]; data_str[7:0] = data_out

  // Notes on the sheet:
  //   Ex 2
  //   Ex 3
  //   Ex 4
  //   Ex 5
endmodule

module mem_rom (
  input  [6:0] addr,
  output [15:0] instruction
);

  wire [15:0] mux0, mux1, mux2, mux3, undriven, undriven_2, undriven_3, undriven_4, undriven_5, undriven_6,
       undriven_7, undriven_8, undriven_9, undriven_10, undriven_11, undriven_12, undriven_13, undriven_14,
       undriven_15, undriven_16, undriven_17, undriven_18, undriven_19, undriven_20, undriven_21,
       undriven_22, undriven_23, undriven_24, undriven_25, undriven_26, undriven_27, undriven_28,
       undriven_29, undriven_30, undriven_31, undriven_32, undriven_33, undriven_34, undriven_35,
       undriven_36, undriven_37, undriven_38, undriven_39;

  Multiplexer #(.select(5), .width(16)) multiplexer_1 (
    .in0(16'h8007), .in1(16'hee08), .in2(16'hee12), .in3(16'hee4a), .in4(16'hee51), .in5(16'hee2d),
    .in6(16'hee41), .in7(16'hbffb), .in8(16'h8a01), .in9(16'h8c8c), .in10(16'hdb80), .in11(16'h8204),
    .in12(16'h8aa0), .in13(16'hc540), .in14(16'h8a80), .in15(16'hc740), .in16(16'h880f), .in17(16'hfe00),
    .in18(16'h8c01), .in19(16'h1930), .in20(16'h8cc8), .in21(16'hcb80), .in22(16'h8c01), .in23(16'h1da8),
    .in24(16'ha805), .in25(16'h8c02), .in26(16'h1da8), .in27(16'ha808), .in28(16'hfe00), .in29(16'h8c01),
    .in30(16'h1030), .in31(16'ha402), .out(mux0), .sel(addr[4:0]));  // open: en
  Multiplexer #(.select(5), .width(16)) multiplexer_2 (
    .in0(16'hfe00), .in1(16'h8000), .in2(16'hfe00), .in3(16'h8c01), .in4(16'ha30), .in5(16'h8c10),
    .in6(16'h1d70), .in7(16'ha804), .in8(16'h8c00), .in9(16'h170), .in10(16'hfe00), .in11(16'h800f),
    .in12(16'hfe00), .in13(16'h8c01), .in14(16'h1b30), .in15(16'h1c68), .in16(16'ha802), .in17(16'hfe00),
    .in18(16'h1a10), .in19(16'ha404), .in20(16'h1ac0), .in21(16'ha402), .in22(16'hfe00), .in23(16'h8a01),
    .in24(16'h8c96), .in25(16'hdb80), .in26(16'hee51), .in27(16'h8a00), .in28(16'h8c96), .in29(16'hdb80),
    .in30(16'h8007), .in31(16'h8e01), .out(mux1), .sel(addr[4:0]));  // open: en
  Multiplexer #(.select(5), .width(16)) multiplexer_3 (
    .in0(16'hfe00), .in1(16'h8a02), .in2(16'h1d28), .in3(16'ha802), .in4(16'hfe00), .in5(16'h8a01),
    .in6(16'h8cb4), .in7(16'hdb80), .in8(16'h8e01), .in9(16'hfe00), .in10(16'h8adc), .in11(16'hd940),
    .in12(16'h8ae6), .in13(16'hd140), .in14(16'h8af0), .in15(16'hd340), .in16(16'hfe00), .in17(16'h8c00),
    .in18(16'h8a01), .in19(16'hda8), .in20(16'h8a2a), .in21(16'h1ba8), .in22(16'ha802), .in23(16'hbffb),
    .in24(16'hfe00), .in25(undriven_20), .in26(undriven), .in27(undriven_21), .in28(undriven_2),
    .in29(undriven_22), .in30(undriven_3), .in31(undriven_23), .out(mux2), .sel(addr[4:0]));  // open: en
  Multiplexer #(.select(5), .width(16)) multiplexer_4 (
    .in0(undriven_4), .in1(undriven_24), .in2(undriven_5), .in3(undriven_25), .in4(undriven_6),
    .in5(undriven_26), .in6(undriven_7), .in7(undriven_27), .in8(undriven_8), .in9(undriven_28),
    .in10(undriven_9), .in11(undriven_29), .in12(undriven_10), .in13(undriven_30), .in14(undriven_11),
    .in15(undriven_31), .in16(undriven_12), .in17(undriven_32), .in18(undriven_13), .in19(undriven_33),
    .in20(undriven_14), .in21(undriven_34), .in22(undriven_15), .in23(undriven_35), .in24(undriven_16),
    .in25(undriven_36), .in26(undriven_17), .in27(undriven_37), .in28(undriven_18), .in29(undriven_38),
    .in30(undriven_19), .in31(undriven_39), .out(mux3), .sel(addr[4:0]));  // open: en
  Multiplexer #(.select(2), .width(16)) multiplexer_5 (
    .in0(mux0), .in1(mux1), .in2(mux2), .in3(mux3), .out(instruction), .sel(addr[6:5]));  // open: en
  // Probe on instruction

  // Other names for the same wires on the sheet: sel[1:0] = addr[6:5]
endmodule

module obstacle_gen (
  input  clk,
  input  rst,
  input  w_en,
  output [3:0] h_bottom,
  output [3:0] h_top
);

  wire [2:0] random_1_out;
  wire [3:0] multiplexer_1_out, multiplexer_2_out;

  Random #(.width(3)) random_1 (.clr(rst), .next(1'b1), .clk(clk), .out(random_1_out));
  Register #(.width(4)) register_1 (.D(multiplexer_1_out), .en(w_en), .clk(clk), .Q(h_bottom), .clr(rst));
  Multiplexer #(.select(3), .width(4), .enable("false")) multiplexer_1 (
    .in0(4'b0001), .in1(4'b0110), .in2(4'b1011), .in3(4'b0111), .in4(4'b0100), .in5(4'b1000), .in6(4'b0010),
    .in7(4'b1010), .out(multiplexer_1_out), .sel(random_1_out));
  Register #(.width(4)) register_2 (.D(multiplexer_2_out), .en(w_en), .clk(clk), .Q(h_top), .clr(rst));
  Multiplexer #(.select(3), .width(4), .enable("false")) multiplexer_2 (
    .in0(4'b0011), .in1(4'b1000), .in2(4'b1101), .in3(4'b1001), .in4(4'b0110), .in5(4'b1010), .in6(4'b0100),
    .in7(4'b1100), .out(multiplexer_2_out), .sel(random_1_out));
endmodule

module affichage (
  input  rst,
  input  clk,
  input  [3:0] h_bottom_obstacle,
  input  [3:0] h_top_obstacle,
  input  [3:0] v_obstacle,
  input  [3:0] h_joueur,
  input  [3:0] v_joueur,
  input  afficher_fin_jeu,
  output [3:0] h_sync,
  output [3:0] v_sync,
  output [2:0] pixel
);

  wire comparator_1_lt, comparator_2_gt, comparator_3_eq, comparator_4_eq, comparator_5_eq, counter_1_carry,
       counter_2_carry, F, or_1_out, or_2_out, register_1_q;
  wire [1:0] and_2_out;
  wire [2:0] multiplexer_1_out;

  Counter #(.width(4), .max('hf)) counter_1 (
    .clr(rst), .load(1'b0), .up(1'b1), .count(1'b1), .clk(clk), .carry(counter_1_carry), .Q(h_sync));  // open: D
  Counter #(.width(4), .max('hf)) counter_2 (
    .clr(rst), .load(1'b0), .up(1'b1), .count(counter_1_carry), .clk(clk), .carry(counter_2_carry), .Q(v_sync));  // open: D
  and and_1 (F, counter_1_carry, counter_2_carry);
  Comparator #(.width(4), .mode("unsigned")) comparator_1 (
    .a(h_sync), .b(h_bottom_obstacle), .lt(comparator_1_lt));  // open: gt, eq
  Comparator #(.width(4), .mode("unsigned")) comparator_2 (
    .a(h_sync), .b(h_top_obstacle), .gt(comparator_2_gt));  // open: eq, lt
  or or_1 (or_1_out, comparator_1_lt, comparator_2_gt);
  Comparator #(.width(4), .mode("unsigned")) comparator_3 (
    .a(v_sync), .b(v_obstacle), .eq(comparator_3_eq));  // open: gt, lt
  Comparator #(.width(4), .mode("unsigned")) comparator_4 (
    .a(h_sync), .b(h_joueur), .eq(comparator_4_eq));  // open: gt, lt
  Comparator #(.width(4), .mode("unsigned")) comparator_5 (
    .a(v_sync), .b(v_joueur), .eq(comparator_5_eq));  // open: gt, lt
  and and_2 (and_2_out[0], or_1_out, comparator_3_eq);
  and and_3 (and_2_out[1], comparator_4_eq, comparator_5_eq);
  Register #(.width(1)) register_1 (.D(afficher_fin_jeu), .en(or_2_out), .clk(clk), .Q(register_1_q), .clr(rst));
  or or_2 (or_2_out, afficher_fin_jeu, F);
  Multiplexer #(.select(2), .width(3), .enable("false")) multiplexer_1 (
    .in0(3'b001), .in1(3'b100), .in2(3'b111), .out(multiplexer_1_out), .sel(and_2_out));  // open: in3
  Multiplexer #(.width(3), .enable("false")) multiplexer_2 (
    .in0(multiplexer_1_out), .in1(3'b110), .out(pixel), .sel(register_1_q));

  // Other names for the same wires on the sheet: aff = afficher_fin_jeu; C = clk; R = rst
endmodule

module decodeur (
  input  [3:0] data,
  input  [7:0] addr,
  input  clk,
  input  rst,
  output [3:0] v_obstacle,
  output [3:0] h_joueur,
  output [3:0] v_joueur,
  output fin_jeu,
  output w_en_obstacle
);

  wire and_1_out, and_2_out, and_3_out, and_4_out, and_5_out, or_1_out;

  and and_1 (and_1_out, addr[4], ~addr[5], addr[6], addr[7]);  // AND_Gate
  and and_2 (and_2_out, ~addr[4], addr[5], addr[6], addr[7]);  // AND_Gate
  and and_3 (and_3_out, addr[4], addr[5], addr[6], addr[7]);
  and and_4 (and_4_out, addr[4], ~addr[5], ~addr[6], addr[7]);  // AND_Gate
  and and_5 (and_5_out, ~addr[4], ~addr[5], ~addr[6], addr[7]);  // AND_Gate
  or or_1 (or_1_out, and_5_out, w_en_obstacle);
  Register #(.width(4)) register_1 (.D(data), .en(and_1_out), .clk(clk), .Q(v_obstacle), .clr(rst));
  Register #(.width(4)) register_2 (.D(data), .en(and_2_out), .clk(clk), .Q(h_joueur), .clr(rst));
  Register #(.width(4)) register_3 (.D(data), .en(and_3_out), .clk(clk), .Q(v_joueur), .clr(rst));
  Register #(.width(1)) register_4 (.D(data[0]), .en(and_4_out), .clk(clk), .Q(fin_jeu), .clr(rst));
  Register #(.width(1)) register_5 (.D(data[0]), .en(or_1_out), .clk(clk), .Q(w_en_obstacle), .clr(rst));
endmodule

module jeu (
  input  clk,
  input  rst,
  input  up,
  input  down,
  output [3:0] v_sync,
  output [3:0] h_sync,
  output [2:0] pixel
);

  wire and_1_out, cpu_1_w_en, decodeur_1_fin_jeu, decodeur_1_w_en_obstacle, sel_btn, sel_h_bottom;
  wire [3:0] decodeur_1_h_joueur, decodeur_1_v_joueur, decodeur_1_v_obstacle, obstacle_gen_1_h_bottom,
       obstacle_gen_1_h_top;
  wire [7:0] addr, cpu_1_data_out, multiplexer_1_out, multiplexer_2_out, multiplexer_3_out, ram_128_1_d_out;

  // Probe on multiplexer_1_out
  cpu cpu_1 (
    .clk(clk), .rst(rst), .data_in(multiplexer_1_out), .addr_out(addr), .w_en(cpu_1_w_en),
    .data_out(cpu_1_data_out));
  Multiplexer #(.width(8), .enable("false")) multiplexer_1 (
    .in0(ram_128_1_d_out), .in1(multiplexer_2_out), .out(multiplexer_1_out), .sel(addr[7]));
  and and_1 (and_1_out, addr[7], cpu_1_w_en);
  Multiplexer #(.width(8), .enable("false")) multiplexer_2 (
    .in0(multiplexer_3_out), .in1({{6{1'b0}}, down, up}), .out(multiplexer_2_out), .sel(sel_btn));
  Multiplexer #(.width(8), .enable("false")) multiplexer_3 (
    .in0({4'b0000, obstacle_gen_1_h_top}), .in1({4'b0000, obstacle_gen_1_h_bottom}), .out(multiplexer_3_out),
    .sel(sel_h_bottom));
  and and_2 (sel_h_bottom, addr[5], ~addr[6], addr[7]);  // AND_Gate
  and and_3 (sel_btn, ~addr[5], addr[6], addr[7]);  // AND_Gate
  RAM_128 ram_128_1 (.ADDR(addr[6:0]), .WR(and_1_out), .D_in(cpu_1_data_out), .CLK(clk), .D_out(ram_128_1_d_out));
  obstacle_gen obstacle_gen_1 (
    .clk(clk), .rst(rst), .w_en(decodeur_1_w_en_obstacle), .h_bottom(obstacle_gen_1_h_bottom),
    .h_top(obstacle_gen_1_h_top));
  decodeur decodeur_1 (
    .data(cpu_1_data_out[3:0]), .addr(addr), .clk(clk), .rst(rst), .v_obstacle(decodeur_1_v_obstacle),
    .h_joueur(decodeur_1_h_joueur), .v_joueur(decodeur_1_v_joueur), .fin_jeu(decodeur_1_fin_jeu),
    .w_en_obstacle(decodeur_1_w_en_obstacle));
  affichage affichage_1 (
    .rst(rst), .clk(clk), .h_bottom_obstacle(obstacle_gen_1_h_bottom), .h_top_obstacle(obstacle_gen_1_h_top),
    .v_obstacle(decodeur_1_v_obstacle), .h_joueur(decodeur_1_h_joueur), .v_joueur(decodeur_1_v_joueur),
    .afficher_fin_jeu(decodeur_1_fin_jeu), .h_sync(v_sync), .v_sync(h_sync), .pixel(pixel));

  // Other names for the same wires on the sheet: btn[1:0] = {down, up}
endmodule
