// Logisim project RAM_synch.circ as structural Verilog: 2 circuits, main circuit RAM_128
module RAM_128 (
  input  [6:0] ADDR,
  input  WR,
  input  [7:0] D_in,
  input  CLK,
  output [7:0] D_out
);

  wire decoder_1_out0, decoder_1_out1, decoder_1_out2, decoder_1_out3, decoder_1_out4, decoder_1_out5,
       decoder_1_out6, decoder_1_out7;
  wire [7:0] ram_16_1_d_out, ram_16_2_d_out, ram_16_3_d_out, ram_16_4_d_out, ram_16_5_d_out, ram_16_6_d_out,
       ram_16_7_d_out, ram_16_8_d_out;

  Decoder #(.select(3)) decoder_1 (
    .out0(decoder_1_out0), .out1(decoder_1_out1), .out2(decoder_1_out2), .out3(decoder_1_out3),
    .out4(decoder_1_out4), .out5(decoder_1_out5), .out6(decoder_1_out6), .out7(decoder_1_out7),
    .sel(ADDR[6:4]), .en(WR));
  RAM_16 ram_16_1 (.D_in(D_in), .WE(decoder_1_out0), .Addr(ADDR[3:0]), .CLK(CLK), .D_out(ram_16_1_d_out));
  RAM_16 ram_16_2 (.D_in(D_in), .WE(decoder_1_out1), .Addr(ADDR[3:0]), .CLK(CLK), .D_out(ram_16_2_d_out));
  RAM_16 ram_16_3 (.D_in(D_in), .WE(decoder_1_out2), .Addr(ADDR[3:0]), .CLK(CLK), .D_out(ram_16_3_d_out));
  RAM_16 ram_16_4 (.D_in(D_in), .WE(decoder_1_out3), .Addr(ADDR[3:0]), .CLK(CLK), .D_out(ram_16_4_d_out));
  RAM_16 ram_16_5 (.D_in(D_in), .WE(decoder_1_out4), .Addr(ADDR[3:0]), .CLK(CLK), .D_out(ram_16_5_d_out));
  RAM_16 ram_16_6 (.D_in(D_in), .WE(decoder_1_out5), .Addr(ADDR[3:0]), .CLK(CLK), .D_out(ram_16_6_d_out));
  RAM_16 ram_16_7 (.D_in(D_in), .WE(decoder_1_out6), .Addr(ADDR[3:0]), .CLK(CLK), .D_out(ram_16_7_d_out));
  RAM_16 ram_16_8 (.D_in(D_in), .WE(decoder_1_out7), .Addr(ADDR[3:0]), .CLK(CLK), .D_out(ram_16_8_d_out));
  Multiplexer #(.select(3), .width(8), .enable("false")) multiplexer_1 (
    .in0(ram_16_1_d_out), .in1(ram_16_2_d_out), .in2(ram_16_3_d_out), .in3(ram_16_4_d_out),
    .in4(ram_16_5_d_out), .in5(ram_16_6_d_out), .in6(ram_16_7_d_out), .in7(ram_16_8_d_out), .out(D_out),
    .sel(ADDR[6:4]));
endmodule

module RAM_16 (
  input  [7:0] D_in,
  input  WE,
  input  [3:0] Addr,
  input  CLK,
  output [7:0] D_out
);

  wire dec0, dec1, dec2, dec3, dec4, dec5, dec6, dec7, dec8, dec9, dec10, dec11, dec12, dec13, dec14, dec15;
  wire [7:0] reg0, reg1, reg2, reg3, reg4, reg5, reg6, reg7, reg8, reg9, reg10, reg11, reg12, reg13, reg14,
       reg15;

  Decoder #(.select(4)) decoder_1 (
    .out0(dec0), .out1(dec1), .out2(dec2), .out3(dec3), .out4(dec4), .out5(dec5), .out6(dec6), .out7(dec7),
    .out8(dec8), .out9(dec9), .out10(dec10), .out11(dec11), .out12(dec12), .out13(dec13), .out14(dec14),
    .out15(dec15), .sel(Addr), .en(WE));
  Register register_1 (.D(D_in), .en(dec8), .clk(CLK), .Q(reg8));  // open: clr
  Register register_2 (.D(D_in), .en(dec9), .clk(CLK), .Q(reg9));  // open: clr
  Register register_3 (.D(D_in), .en(dec10), .clk(CLK), .Q(reg10));  // open: clr
  Register register_4 (.D(D_in), .en(dec11), .clk(CLK), .Q(reg11));  // open: clr
  // Probe on reg8
  // Probe on reg9
  // Probe on reg10
  // Probe on reg11
  Register register_5 (.D(D_in), .en(dec12), .clk(CLK), .Q(reg12));  // open: clr
  Register register_6 (.D(D_in), .en(dec13), .clk(CLK), .Q(reg13));  // open: clr
  Register register_7 (.D(D_in), .en(dec14), .clk(CLK), .Q(reg14));  // open: clr
  Register register_8 (.D(D_in), .en(dec15), .clk(CLK), .Q(reg15));  // open: clr
  // Probe on reg12
  // Probe on reg13
  // Probe on reg14
  // Probe on reg15
  Register register_9 (.D(D_in), .en(dec0), .clk(CLK), .Q(reg0));  // open: clr
  Register register_10 (.D(D_in), .en(dec1), .clk(CLK), .Q(reg1));  // open: clr
  Register register_11 (.D(D_in), .en(dec2), .clk(CLK), .Q(reg2));  // open: clr
  Register register_12 (.D(D_in), .en(dec3), .clk(CLK), .Q(reg3));  // open: clr
  // Probe on reg0
  // Probe on reg1
  // Probe on reg2
  // Probe on reg3
  Register register_13 (.D(D_in), .en(dec4), .clk(CLK), .Q(reg4));  // open: clr
  Register register_14 (.D(D_in), .en(dec5), .clk(CLK), .Q(reg5));  // open: clr
  Register register_15 (.D(D_in), .en(dec6), .clk(CLK), .Q(reg6));  // open: clr
  Register register_16 (.D(D_in), .en(dec7), .clk(CLK), .Q(reg7));  // open: clr
  // Probe on reg4
  // Probe on reg5
  // Probe on reg6
  // Probe on reg7
  Multiplexer #(.select(4), .width(8), .enable("false")) multiplexer_1 (
    .in0(reg0), .in1(reg1), .in2(reg2), .in3(reg3), .in4(reg4), .in5(reg5), .in6(reg6), .in7(reg7),
    .in8(reg8), .in9(reg9), .in10(reg10), .in11(reg11), .in12(reg12), .in13(reg13), .in14(reg14),
    .in15(reg15), .out(D_out), .sel(Addr));
  // Probe on D_out

  // Other names for the same wires on the sheet: clock = CLK; data_write[7:0] = D_in
endmodule
